# Fritzing sketch Connection (saved by Fritzing 0.9.6b)
breadboards: 1

parts:
  WeMos_D1_Mini1 = WeMos D1 Mini
  R10 = Resistor [tolerance=±5% power=0.25 resistance=1k package=THT]  # not connected
  R11 = Resistor [tolerance=±5% power=0.25 resistance=3.3k package=THT]  # not connected
  R12 = Resistor [tolerance=±5% resistance=8.2k power=0.25 package=THT]  # not connected
  Q1 = Basic FET P-Channel [part_number=L7805ABV package="TO220 [THT]"]
  Q3 = NPN-Transistor [part_number=BC546 package="TO92 [THT]"]  # not connected
  C11 = Ceramic Capacitor [capacitance=0.1mF voltage=35V package="100 mil [THT, multilayer]"]  # not connected
  R7 = Resistor [tolerance=±5% power=0.25 resistance=4.7k package=THT]
  R8 = Resistor [tolerance=±5% power=0.25 resistance=1.8 package=THT]  # not connected
  D2 = Rectifier Diode [part_number=1N5408 package="300 mil [THT]"]  # not connected
  C10 = Ceramic Capacitor [capacitance=0.47mF voltage=35V package="100 mil [THT, multilayer]"]
  Q2 = NPN-Transistor [part_number=BC546 package="TO92 [THT]"]  # not connected
  D1 = Rectifier Diode [part_number=1N4004 package="300 mil [THT]"]  # not connected
  R2 = Resistor [tolerance=±5% power=0.25 resistance=8.2k package=THT]  # not connected
  R9 = Resistor [tolerance=±5% power=0.25 resistance=1.8 package=THT]  # not connected
  D4 = Rectifier Diode [part_number=1N4004 package="300 mil [THT]"]  # not connected
  D5 = Rectifier Diode [part_number=1N4004 package="300 mil [THT]"]  # not connected
  C12 = Ceramic Capacitor [capacitance=0.47mF voltage=35V package="100 mil [THT, multilayer]"]

nets:
  N1: WeMos_D1_Mini1.RX, R7.Pin_0
  N2: Q1.gate, Q1.drain, C10.0, C10.1, C12.0
  N3: Q1.source, R7.Pin_1

notes:
  1.8 om
  1 kom
  4.7 kom
  8.2 kom
  1N4004
  1N5408
  1N5817
  100 kom
  0.15 µF
  2.2 µF
  1.5 µF
  Зуммер
  Микрофон
